# Fritzing sketch Connection (saved by Fritzing 0.9.3b)
circuit board: 8.46667cm x 5.64444cm
breadboards: 1

parts:
  SparkFun_Pro_Micro1 = SparkFun Pro Micro [part_number=DEV-12640]
  MD03A1 = Dual VNH2SP30 Motor Driver [part_number=MD03A]
  JP1 = Header 3 [package=molex-1x3_lock]
  DS1 = DS18B20 1-Wire Temperature Sensor [part_number=DS18B20]
  M1 = DC Motor
  R1 = Resistor [tolerance=±5% resistance=220 package="1206 [SMD]"]

nets:
  N1: SparkFun_Pro_Micro1.RAW, MD03A1.VIN, JP1.3
  GND: SparkFun_Pro_Micro1.GND, MD03A1.GND, JP1.1, DS1.GND
  VCC: SparkFun_Pro_Micro1.VCC, MD03A1.+5V_(IN), DS1.VDD, R1.Pin_0
  N2: SparkFun_Pro_Micro1.SCK, DS1.DQ, R1.Pin_1
  N3: SparkFun_Pro_Micro1.D6, JP1.2
  N4: SparkFun_Pro_Micro1.D5, MD03A1.PWM
  N5: MD03A1.OUT_1A, M1.pin_1
  N6: MD03A1.OUT_1B, M1.pin_2

custom parts:
  SparkFun Pro Micro: This tiny little board does all of the neat-o Arduino tricks that you’re familiar with: 4 channels of 10-bit ADC, 5 PWM pins, 12 DIOs as well as hardware serial connections Rx and Tx. Running at 16MHz and 5V, this board will remind you a lot of your other favorite Arduino-compatible boards but this little guy can go just about anywhere. There is a voltage regulator on board so it can accept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
